# Fritzing sketch VaporizR2 (saved by Fritzing 0.9.3b)
circuit board: 8.46667cm x 5.64444cm

parts:
  Arduino_Nano = Arduino Nano (Rev3.0)
  Part2 = Motor Driver 1A Dual TB6612FNG
  Bluetooth = Bluetooth HC-05 Macho
  MotorA = DC Motor
  MotorB = DC Motor
  VCC2 = 4 x AAA Battery Mount
  S1 = Toggle Switch [package=THT]
  VCC3 = Battery block 9V
  LED1 = LED - 5mm [color="Red (633nm)" package="5 mm [THT]"]
  LED2 = LED - 5mm [color="Red (633nm)" package="5 mm [THT]"]
  LED3 = LEDs [package=led10mm]
  LED4 = LEDs [package=led10mm]
  J1 = Piezo Speaker

nets:
  N1: Arduino_Nano.D2, Bluetooth.RXD
  N2: Arduino_Nano.D3, Bluetooth.TXD
  N3: Arduino_Nano.D4, Part2.AIN1
  N4: Arduino_Nano.D5, Part2.AIN2
  N5: Arduino_Nano.D6, Part2.STBY
  N6: Arduino_Nano.D7, Part2.BIN2
  N7: Arduino_Nano.D8, Part2.BIN1
  N8: Arduino_Nano.D9, LED3.C, LED4.C
  N9: Arduino_Nano.D10, Part2.PWMB
  N10: Arduino_Nano.D11/MOSI, Part2.PWMA
  N11: Arduino_Nano.D12/MISO, J1.pin2
  N12: Arduino_Nano.VIN, S1.L1
  GND: Arduino_Nano.GND, Part2.GND, Bluetooth.GND, VCC2.-, VCC3.-, LED1.anode, LED2.anode, LED3.A, LED4.A, J1.pin1
  VCC: Arduino_Nano.5V, Part2.VCC, Bluetooth.VCC
  N13: Arduino_Nano.D13/SCK, LED1.cathode
  N14: Part2.B01, MotorB.pin_1
  N15: Part2.B02, MotorB.pin_2
  N16: Part2.A02, MotorA.pin_1
  N17: Part2.A01, MotorA.pin_2
  N18: Part2.VM, VCC2.+
  N19: Bluetooth.State, LED2.cathode
  N20: S1.COM, VCC3.+
